# Fritzing sketch notamp03 (saved by Fritzing 0.9.2b)
perfboards: 2

parts:
  IC1 = DIP - 20 pins [chip_label=AtTiny2313-20PU package="DIP (Dual Inline) [THT]"]
  U1 = USB UART [package=ssop28db]
  IC2 = DIP - 8 pins [chip_label=MCP3002 package="DIP (Dual Inline) [THT]"]
  U2 = POT_SWITCH [package=pot_pth_switch]
  U3 = POT [package=pot_alpha_rv16af-20]
  R1 = Resistor [tolerance=±5% resistance=220 package=THT]
  LED1 = smd LED [color="Green (555nm)" package="0603 [SMD]"]
  R2 = Resistor [tolerance=±5% resistance=220 package=THT]
  S1 = Pushbutton [package="[SMD]"]
  C1 = Capacitor [package=cap-pth-small-kit]
  R3 = Resistor [tolerance=±5% resistance=220 package=THT]
  LED2 = smd LED [color="Yellow (595nm)" package="0603 [SMD]"]  # not connected
  R4 = Trimmer Potentiometer [maximum_resistance=10kΩ package=THT]

nets:
  N1: IC1.PA2_(!RESET), R2.Pin_1, S1.Pin_1, S1.Pin_2
  N2: IC1.PD0_(RXD), U1.TXD
  N3: IC1.PD1_(TXD), U1.RXD
  N4: IC1.PA1_(XTAL2), U1.RTS
  N5: IC1.PA0_(XTAL1), U1.CTS
  N6: IC1.PD5_(OC0B/T1), R1.Pin_0
  N7: IC1.GND, U1.TEST, IC2.pin4, U2.G$1_A, U2.G$1_S, U3.A, LED1.anode, S1.Pin_3, S1.Pin_4, C1.1, R4.leg1
  N8: IC1.PB2_(OC0A/PCINT2), R4.leg2
  N9: IC1.PB3_(OC1A/PCINT3), U2.G$1_E
  N10: IC1.PB4_(OC1B/PCINT4), IC2.pin1
  N11: IC1.PB5_(MOSI/DI/SDA/PCINT5), IC2.pin5
  N12: IC1.PB6_(MISO/DO/PCINT6), IC2.pin6
  N13: IC1.PB7_(UCSK/SCL/PCINT7), IC2.pin7
  N14: IC1.VCC, U1.USBDM, IC2.pin8, U2.G$2_2, U3.E, R2.Pin_0, C1.2, R3.Pin_0
  N15: IC2.pin2, U3.S
  N16: IC2.pin3, U2.G$2_1
  N17: R1.Pin_1, LED1.cathode

notes:
  Relay-Switch
  VU-Meter
  Umber-LED
  (VU-Meter)

custom parts:
  DIP - 20 pins: A DIP stand-in part for whatever IC you want. With 20 pins on a 300mil dual inline package (DIP) footprint.
  DIP - 8 pins: A DIP stand-in part for whatever IC you want. With 8 pins on a 300mil dual inline package (DIP) footprint.
